# Fritzing sketch alchemist (saved by Fritzing 0.9.2b)
breadboards: 1

parts:
  IC1 = Voltage Regulator [package=to220-igo]
  D1 = Diode [package=diode-1n4148]
  C1 = Ceramic Capacitor [capacitance=100nF package="100 mil [THT, multilayer]"]  # not connected
  C2 = Ceramic Capacitor [capacitance=100nF package="100 mil [THT, multilayer]"]  # not connected

nets:
  N1: IC1.GND, D1.A
